# Fritzing sketch EE3579_LAB3_Closed_Loop (saved by Fritzing 0.9.3b)
breadboards: 1

parts:
  U1 = 74HC04_HEX_INVERTER [package=dil14]
  IC2 = L293D [package=THT]
  M1 = DC Motor
  Part1 = Arduino Uno (Rev3)
  3-pins_Hall_Effect_Sensor1 = mystery part, 3 pins [chip_label="Hall Effect Sensor"]
  M2 = DC Motor
  3-pins_Hall_Effect_Sensor3 = mystery part, 3 pins [chip_label="Hall Effect Sensor"]

nets:
  GND: U1.GND, IC2.0V, Part1.GND, 3-pins_Hall_Effect_Sensor1.pin1, 3-pins_Hall_Effect_Sensor3.pin1
  N1: U1.6Y, IC2.In_3, Part1.D5_PWM
  N2: U1.6A, IC2.In_4, Part1.D7
  VCC: U1.VCC, IC2.+Vmotor, IC2.+V, Part1.5V, 3-pins_Hall_Effect_Sensor1.pin2, 3-pins_Hall_Effect_Sensor3.pin2
  N3: IC2.In_1, Part1.D10_PWM/SS
  N4: IC2.Out_1_(_Controlled_by_Enable_1_), M1.pin_2
  N5: IC2.Out_2_(_Controlled_by_Enable_1_), M1.pin_1
  N6: IC2.In_2, Part1.D8
  N7: IC2.Out_3_(_Controlled_by_Enable_2_), M2.pin_1
  N8: IC2.Out_4_(_Controlled_by_Enable_2_), M2.pin_2
  N9: Part1.D2, 3-pins_Hall_Effect_Sensor3.pin3
  N10: Part1.D3_PWM, 3-pins_Hall_Effect_Sensor1.pin3
